// Logisim project MIPS-logisim.circ as structural Verilog: 13 circuits, main circuit adder32
module adder32 (
  input  in_Cin,
  input  [31:0] in_A,
  input  [31:0] in_B,
  output [31:0] out_F,
  output out_SF,
  output out_CF,
  output out_ZF,
  output out_OF
);

  wire adder_1_cout, adder_2_cout, adder_3_cout, adder_4_cout;

  Adder adder_1 (.a(in_A[7:0]), .b(in_B[7:0]), .out(out_F[7:0]), .cin(in_Cin), .cout(adder_1_cout));
  Adder adder_2 (.a(in_A[15:8]), .b(in_B[15:8]), .out(out_F[15:8]), .cin(adder_1_cout), .cout(adder_2_cout));
  Adder adder_3 (.a(in_A[23:16]), .b(in_B[23:16]), .out(out_F[23:16]), .cin(adder_2_cout), .cout(adder_3_cout));
  Adder adder_4 (.a(in_A[31:24]), .b(in_B[31:24]), .out(out_F[31:24]), .cin(adder_3_cout), .cout(adder_4_cout));
  xor a (out_OF, adder_4_cout, adder_3_cout);
  mux8_msb msb (.data(out_F[31:24]), .result(out_SF));
  nor32 c (.in0(out_F[7:0]), .in1(out_F[15:8]), .in2(out_F[23:16]), .in3(out_F[31:24]), .result(out_ZF));
  xor b (out_CF, in_Cin, adder_4_cout);

  // Notes on the sheet:
  //   fork3,8 deleted
  //   0
  //   0
  //   1
  //   2
  //   1
  //   7
  //   3
  //   2
  //   4
  //   5
  //   6
endmodule

module nor32 (
  input  [7:0] in0,
  input  [7:0] in1,
  input  [7:0] in2,
  input  [7:0] in3,
  output result
);

  wire or_2_out;
  wire [7:0] or_1_out;

  assign or_1_out = in0 | in1 | in2 | in3;  // OR_Gate or_1, 8 bits wide
  or or_2 (or_2_out, or_1_out[0], or_1_out[1], or_1_out[2], or_1_out[3], or_1_out[4], or_1_out[5], or_1_out[6], or_1_out[7]);
  not not_1 (result, or_2_out);
endmodule

module mux8_msb (
  input  [7:0] data,
  output result
);

  BitSelector bitselector_1 (.in(data), .out(result), .sel(3'b111));
endmodule

module ALU (
  input  [4:0] in_shamt,
  input  [31:0] in_A,
  input  [31:0] in_B,
  input  [2:0] ALUctr,
  output out_Zero,
  output out_Overflow,
  output [31:0] out_Result
);

  wire Adder_out_cf, Adder_out_of, Adder_out_sf, ALU_decoder_ov, ALU_decoder_sig, ALU_decoder_sub,
       multiplexer_3_out, xor_2_out, xor_3_out;
  wire [1:0] ALU_decoder_op;
  wire [31:0] Adder_out_f, bit_extender_1_out, multiplexer_1_out, or_1_out, shifter_1_out, xor_1_out;

  ALU_dec ALU_decoder (
    .in_op(ALUctr), .SUB(ALU_decoder_sub), .OV(ALU_decoder_ov), .SIG(ALU_decoder_sig), .OP(ALU_decoder_op));
  assign bit_extender_1_out = {{31{ALU_decoder_sub}}, ALU_decoder_sub};  // Bit_Extender bit_extender_1
  assign xor_1_out = in_B ^ bit_extender_1_out;  // XOR_Gate xor_1, 32 bits wide
  assign or_1_out = in_A | in_B;  // OR_Gate or_1, 32 bits wide
  adder32 Adder (
    .in_Cin(ALU_decoder_sub), .in_A(in_A), .in_B(xor_1_out), .out_F(Adder_out_f), .out_SF(Adder_out_sf),
    .out_CF(Adder_out_cf), .out_ZF(out_Zero), .out_OF(Adder_out_of));
  Multiplexer #(.width(32)) multiplexer_1 (
    .in0({32{1'b0}}), .in1(32'h1), .out(multiplexer_1_out), .sel(multiplexer_3_out));
  Shifter #(.width(32)) shifter_1 (.in(in_B), .\dist (in_shamt), .out(shifter_1_out));
  xor xor_2 (xor_2_out, ALU_decoder_sub, Adder_out_cf);
  xor xor_3 (xor_3_out, Adder_out_sf, Adder_out_of);
  Multiplexer #(.select(2), .width(32)) multiplexer_2 (
    .in0(Adder_out_f), .in1(or_1_out), .in2(multiplexer_1_out), .in3(shifter_1_out), .out(out_Result),
    .sel(ALU_decoder_op));
  Multiplexer multiplexer_3 (.in0(xor_2_out), .in1(xor_3_out), .out(multiplexer_3_out), .sel(ALU_decoder_sig));
  and and_1 (out_Overflow, Adder_out_of, ALU_decoder_ov);
endmodule

module ALU_dec (
  input  [2:0] in_op,
  output SUB,
  output OV,
  output SIG,
  output [1:0] OP
);

  wire i_add_out, i_addu_out, i_or_out, i_sll_out, i_slt_out, i_sltu_out, i_sub_out, i_subu_out, not_1_out,
       not_2_out, not_3_out, not_4_out, not_5_out, not_6_out, not_7_out, not_8_out, not_9_out, not_10_out,
       not_11_out, not_12_out;

  not not_1 (not_1_out, in_op[2]);
  not not_2 (not_2_out, in_op[1]);
  not not_3 (not_3_out, in_op[0]);
  not not_4 (not_4_out, in_op[2]);
  and i_addu (i_addu_out, not_1_out, not_2_out, not_3_out);
  not not_5 (not_5_out, in_op[1]);
  not not_6 (not_6_out, in_op[2]);
  and i_add (i_add_out, not_4_out, not_5_out, in_op[0]);
  and i_or (i_or_out, not_6_out, in_op[1], not_7_out);
  not not_7 (not_7_out, in_op[0]);
  not not_8 (not_8_out, in_op[1]);
  not not_9 (not_9_out, in_op[0]);
  and i_subu (i_subu_out, in_op[2], not_8_out, not_9_out);
  not not_10 (not_10_out, in_op[1]);
  and i_sub (i_sub_out, in_op[2], not_10_out, in_op[0]);
  not not_11 (not_11_out, in_op[0]);
  and i_sltu (i_sltu_out, in_op[2], in_op[1], not_11_out);
  and i_slt (i_slt_out, in_op[2], in_op[1], in_op[0]);
  not not_12 (not_12_out, in_op[2]);
  and i_sll (i_sll_out, not_12_out, in_op[1], in_op[0]);
  or or_1 (SUB, i_subu_out, i_sub_out, i_sltu_out, i_slt_out);
  or or_2 (OV, i_add_out, i_sub_out);
  buf or_3 (SIG, i_slt_out);  // OR_Gate
  or or_4 (OP[0], i_or_out, i_sll_out);
  or or_5 (OP[1], i_sltu_out, i_slt_out, i_sll_out);
endmodule

module instr_fetch (
  input  clk,
  input  [15:0] in_imm16,
  input  clr,
  input  in_Branch,
  input  in_Zero,
  output [31:0] instr,
  output [5:0] instr_func,
  output [4:0] instr_shamt,
  output [4:0] instr_Rd,
  output [4:0] instr_Rt,
  output [4:0] instr_Rs,
  output [5:0] instr_Op,
  output [15:0] instr_Imm16,
  output [25:0] instr_target
);

  wire [0:0] and_1_out;
  wire [7:0] bit_extender_2_out;
  wire [29:0] adder_1_out, adder_2_out, bit_extender_1_out, multiplexer_1_out, PC_q;

  Register #(.width(30)) PC (.D(multiplexer_1_out), .clk(clk), .Q(PC_q));  // open: en, clr
  Adder #(.width(30)) adder_1 (.a(PC_q), .b(30'h1), .out(adder_1_out));  // open: cin, cout
  assign bit_extender_1_out = {{14{in_imm16[15]}}, in_imm16};  // Bit_Extender bit_extender_1
  Adder #(.width(30)) adder_2 (.a(adder_1_out), .b(bit_extender_1_out), .out(adder_2_out));  // open: cin, cout
  Multiplexer #(.select(2), .width(30)) multiplexer_1 (
    .in0(adder_1_out), .in1(adder_2_out), .in2({30{1'b0}}), .in3({30{1'b0}}), .out(multiplexer_1_out),
    .sel({clr, and_1_out[0]}));
  and and_1 (and_1_out[0], in_Branch, in_Zero);
  Bit_Extender #(.in_width(30), .out_width(8)) bit_extender_2 (.in(PC_q), .out(bit_extender_2_out));
  RAM #(.dataWidth(32)) ram_1 (.addr(bit_extender_2_out), .clk(clk), .dout(instr));  // open: we, oe, din

  assign instr_func = instr[5:0];
  assign instr_Imm16 = instr[15:0];
  assign instr_Op = instr[31:26];
  assign instr_Rd = instr[15:11];
  assign instr_Rs = instr[25:21];
  assign instr_Rt = instr[20:16];
  assign instr_shamt = instr[10:6];
  assign instr_target = instr[25:0];
endmodule

module main (
  input  in_1,
  output [31:0] out_2,
  output [31:0] out_3,
  output [31:0] out_4,
  output [31:0] out_5,
  output [31:0] out_6
);

  wire and_2_out, and_3_out, and_4_out, and_7_out, and_8_out, and_9_out, and_10_out, BrP_Br, BrPredictor_out,
       BrPredictor_result, BrPredictor_WE, clk_brp, comparator_1_eq, comparator_2_eq, comparator_3_eq,
       comparator_4_eq, Ex_Branch, Ex_Jump, Ex_Mem2Reg, Ex_MemWr, Ex_Nzero, Ex_Overflow, Ex_RegWr, Ex_Zero,
       FlushEx, fwEx_flag, fwMem_flag, ID_ALUimm, ID_Branch, ID_ExtOp, ID_Jump, ID_Mem2Reg, ID_MemWr,
       ID_Nzero, ID_RegWr, inEx_Mem2Reg, inEx_MemWr, Mem_RegWr, multiplexer_1_out, multiplexer_2_out,
       multiplexer_5_out, multiplexer_9_out, multiplexer_10_out, not_1_out, not_2_out, not_3_out, not_4_out,
       or_1_out, RegDst, register_4_q, register_5_q, register_8_q, register_15_q, register_16_q,
       register_28_q, register_29_q, register_39_q, Wr_RegWr, xor_1_out;
  wire [2:0] ID_ALUctl, register_22_q;
  wire [4:0] Ex_Rw, ID_Rw, Mem_Rw, register_23_q, Wr_Rw;
  wire [5:0] func;
  wire [7:0] bit_extender_1_out, bit_extender_3_out;
  wire [15:0] register_21_q;
  wire [15:6] ID_imm16;
  wire [25:0] Ex_nextpc;
  wire [25:16] ID_jmptar;
  wire [29:0] bit_extender_2_out, bit_extender_4_out, BrP_target, Ex_btarget, Ex_jtarget, ID_nextpc,
       IF_nextpc, Mem_target, multiplexer_3_out, multiplexer_6_out, multiplexer_8_out, PC_q, register_6_q,
       register_7_q, register_12_q;
  wire [31:0] Ex_ALUout, Ex_BusB, ext_mux_1_out_32, fwMem_ALUout, ID_BusA, ID_BusB, inEx_BusB, Mem_BusW,
       multiplexer_4_out, multiplexer_13_out, multiplexer_14_out, multiplexer_17_out, reg32_1_out_ra,
       reg32_1_out_rb, register_11_q, register_19_q, register_38_q, Wr_data;
  wire [31:26] instr;

  Multiplexer multiplexer_1 (.in0(Ex_Jump), .in1(1'b0), .out(multiplexer_1_out), .sel(FlushEx));
  Multiplexer multiplexer_2 (.in0(Ex_Branch), .in1(1'b0), .out(multiplexer_2_out), .sel(FlushEx));
  Multiplexer #(.width(30)) multiplexer_3 (
    .in0(multiplexer_6_out), .in1(Mem_target), .out(multiplexer_3_out), .sel(FlushEx));
  Register #(.trigger("falling"), .width(30)) PC (
    .D(multiplexer_3_out), .clk(clk_brp), .Q(PC_q), .clr(in_1));  // open: en
  Register #(.trigger("falling"), .width(32)) register_1 (
    .D(Ex_ALUout), .clk(clk_brp), .Q(fwMem_ALUout));  // open: en, clr
  Register #(.trigger("falling"), .width(1)) register_2 (
    .D(Ex_Mem2Reg), .clk(clk_brp), .Q(inEx_Mem2Reg));  // open: en, clr
  Register #(.trigger("falling"), .width(5)) register_3 (.D(Ex_Rw), .clk(clk_brp), .Q(Mem_Rw));  // open: en, clr
  Register #(.trigger("falling"), .width(1)) register_4 (
    .D(Ex_Nzero), .clk(clk_brp), .Q(register_4_q));  // open: en, clr
  Register #(.trigger("falling"), .width(1)) register_5 (
    .D(Ex_Zero), .clk(clk_brp), .Q(register_5_q));  // open: en, clr
  Register #(.trigger("falling"), .width(30)) register_6 (
    .D(Ex_btarget), .clk(clk_brp), .Q(register_6_q));  // open: en, clr
  Register #(.trigger("falling"), .width(30)) register_7 (
    .D(Ex_jtarget), .clk(clk_brp), .Q(register_7_q));  // open: en, clr
  Register #(.trigger("falling"), .width(1)) register_8 (
    .D(multiplexer_1_out), .clk(clk_brp), .Q(register_8_q));  // open: en, clr
  Register #(.trigger("falling"), .width(1)) register_9 (
    .D(multiplexer_2_out), .clk(clk_brp), .Q(BrPredictor_WE));  // open: en, clr
  Multiplexer #(.width(32)) multiplexer_4 (.in0(out_2), .in1({32{1'b0}}), .out(multiplexer_4_out), .sel(or_1_out));
  or or_1 (or_1_out, BrP_Br, FlushEx);
  not not_1 (not_1_out, register_5_q);
  Multiplexer multiplexer_5 (.in0(register_5_q), .in1(not_1_out), .out(multiplexer_5_out), .sel(register_4_q));
  Multiplexer #(.width(30)) multiplexer_6 (.in0(IF_nextpc), .in1(BrP_target), .out(multiplexer_6_out), .sel(BrP_Br));
  Register #(.trigger("falling"), .width(30)) register_10 (
    .D(IF_nextpc), .clk(clk_brp), .Q(ID_nextpc));  // open: en, clr
  Register #(.trigger("falling"), .width(32)) register_11 (
    .D(multiplexer_4_out), .clk(clk_brp), .Q(register_11_q));  // open: en, clr
  mips_decoder mips_decoder_1 (
    .in_op(instr), .in_func(func), .RegWr(ID_RegWr), .ALUsrc(ID_ALUimm), .RegDst(RegDst),
    .MemtoReg(ID_Mem2Reg), .MemWr(ID_MemWr), .Branch(ID_Branch), .Nzero(ID_Nzero), .Jump(ID_Jump),
    .ExtOp(ID_ExtOp), .ALUctl(ID_ALUctl));  // open: Rtype
  Multiplexer #(.width(5)) multiplexer_7 (.in0(ID_jmptar[20:16]), .in1(ID_imm16[15:11]), .out(ID_Rw), .sel(RegDst));
  Register #(.trigger("falling"), .width(30)) register_12 (
    .D({Ex_jtarget[29:26], Ex_nextpc}), .clk(clk_brp), .Q(register_12_q));  // open: en, clr
  Multiplexer #(.width(30)) multiplexer_8 (
    .in0(register_12_q), .in1(register_6_q), .out(multiplexer_8_out), .sel(BrPredictor_result));
  and and_1 (BrPredictor_result, multiplexer_5_out, BrPredictor_WE);
  reg32 reg32_1 (
    .clear(in_1), .in_Ra(ID_jmptar[25:21]), .in_Rb(ID_jmptar[20:16]), .in_Rw(Wr_Rw), .in_WE(Wr_RegWr),
    .in_Rwdata(Wr_data), .clk(clk_brp), .out_Ra(reg32_1_out_ra), .out_Rb(reg32_1_out_rb));
  Multiplexer multiplexer_9 (.in0(Ex_RegWr), .in1(1'b0), .out(multiplexer_9_out), .sel(FlushEx));
  Multiplexer multiplexer_10 (.in0(Ex_Overflow), .in1(1'b0), .out(multiplexer_10_out), .sel(FlushEx));
  xor xor_1 (xor_1_out, BrPredictor_result, BrPredictor_out);
  Multiplexer #(.width(32)) multiplexer_11 (
    .in0(register_11_q), .in1({32{1'b0}}), .out({instr, ID_jmptar, ID_imm16, func}), .sel(FlushEx));
  Register #(.trigger("falling"), .width(32)) register_13 (.D(Ex_BusB), .clk(clk_brp), .Q(inEx_BusB));  // open: en, clr
  Register #(.trigger("falling"), .width(1)) register_14 (
    .D(Ex_MemWr), .clk(clk_brp), .Q(inEx_MemWr));  // open: en, clr
  Register #(.trigger("falling"), .width(1)) register_15 (
    .D(multiplexer_9_out), .clk(clk_brp), .Q(register_15_q));  // open: en, clr
  Register #(.trigger("falling"), .width(1)) register_16 (
    .D(multiplexer_10_out), .clk(clk_brp), .Q(register_16_q));  // open: en, clr
  and and_2 (and_2_out, BrPredictor_WE, xor_1_out);
  Adder #(.width(30)) adder_1 (.a(30'h1), .b(PC_q), .out(IF_nextpc));  // open: cin, cout
  Bit_Extender #(.in_width(30), .out_width(8)) bit_extender_1 (.in(PC_q), .out(bit_extender_1_out));
  Comparator #(.mode("unsigned"), .width(5)) comparator_1 (
    .a(ID_jmptar[25:21]), .b(Mem_Rw), .eq(comparator_1_eq));  // open: gt, lt
  Comparator #(.mode("unsigned"), .width(5)) comparator_2 (
    .a(Mem_Rw), .b(ID_jmptar[20:16]), .eq(comparator_2_eq));  // open: gt, lt
  Multiplexer #(.width(30)) multiplexer_12 (
    .in0(multiplexer_8_out), .in1(register_7_q), .out(Mem_target), .sel(register_8_q));
  RAM #(.asyncread("true"), .dataWidth(32), .trigger("falling")) ram_1 (
    .addr(bit_extender_1_out), .dout(out_2));  // open: we, oe, clk, din
  and and_3 (and_3_out, comparator_1_eq, fwMem_flag);
  and and_4 (and_4_out, fwMem_flag, comparator_2_eq);
  and and_5 (Mem_RegWr, register_15_q, not_2_out);
  not not_2 (not_2_out, register_16_q);
  or or_2 (FlushEx, register_8_q, and_2_out);
  Multiplexer #(.width(32)) multiplexer_13 (
    .in0(reg32_1_out_ra), .in1(fwMem_ALUout), .out(multiplexer_13_out), .sel(and_3_out));
  Multiplexer #(.width(32)) multiplexer_14 (
    .in0(reg32_1_out_rb), .in1(fwMem_ALUout), .out(multiplexer_14_out), .sel(and_4_out));
  Comparator #(.mode("unsigned"), .width(5)) comparator_3 (
    .a(ID_jmptar[25:21]), .b(Ex_Rw), .eq(comparator_3_eq));  // open: gt, lt
  Comparator #(.mode("unsigned"), .width(5)) comparator_4 (
    .a(Ex_Rw), .b(ID_jmptar[20:16]), .eq(comparator_4_eq));  // open: gt, lt
  assign bit_extender_2_out = {{14{ID_imm16[15]}}, {ID_imm16, func}};  // Bit_Extender bit_extender_2
  and and_6 (BrP_Br, ID_Branch, BrPredictor_out);
  Adder #(.width(30)) adder_2 (.a(ID_nextpc), .b(bit_extender_2_out), .out(BrP_target));  // open: cin, cout
  Multiplexer #(.width(32)) multiplexer_15 (.in0(multiplexer_13_out), .in1(Ex_ALUout), .out(ID_BusA), .sel(and_7_out));
  and and_7 (and_7_out, comparator_3_eq, fwEx_flag);
  and and_8 (and_8_out, fwEx_flag, comparator_4_eq);
  Multiplexer #(.width(32)) multiplexer_16 (.in0(multiplexer_14_out), .in1(Ex_ALUout), .out(ID_BusB), .sel(and_8_out));
  Bit_Extender #(.in_width(32), .out_width(8), .\type ("zero")) bit_extender_3 (
    .in(fwMem_ALUout), .out(bit_extender_3_out));
  not not_3 (not_3_out, Ex_Mem2Reg);
  Clock clock_1 (.out(clk_brp));
  RAM #(.dataWidth(32), .trigger("falling")) ram_2 (
    .addr(bit_extender_3_out), .we(inEx_MemWr), .clk(clk_brp), .din(inEx_BusB), .dout(Mem_BusW));  // open: oe
  Register #(.trigger("falling"), .width(1)) register_17 (
    .D(and_9_out), .clk(clk_brp), .Q(fwMem_flag));  // open: en, clr
  and and_9 (and_9_out, Ex_RegWr, not_3_out);
  Register #(.trigger("falling"), .width(30)) register_18 (
    .D(ID_nextpc), .clk(clk_brp), .Q({Ex_jtarget[29:26], Ex_nextpc}));  // open: en, clr
  Register #(.trigger("falling"), .width(32)) register_19 (
    .D(ID_BusA), .clk(clk_brp), .Q(register_19_q));  // open: en, clr
  Register #(.trigger("falling"), .width(32)) register_20 (.D(ID_BusB), .clk(clk_brp), .Q(Ex_BusB));  // open: en, clr
  Register #(.trigger("falling"), .width(16)) register_21 (
    .D({ID_imm16, func}), .clk(clk_brp), .Q(register_21_q));  // open: en, clr
  Register #(.trigger("falling"), .width(3)) register_22 (
    .D(ID_ALUctl), .clk(clk_brp), .Q(register_22_q));  // open: en, clr
  Register #(.trigger("falling"), .width(5)) register_23 (
    .D(ID_imm16[10:6]), .clk(clk_brp), .Q(register_23_q));  // open: en, clr
  and and_10 (and_10_out, ID_RegWr, not_4_out);
  not not_4 (not_4_out, ID_Mem2Reg);
  Register #(.trigger("falling"), .width(1)) register_24 (
    .D(and_10_out), .clk(clk_brp), .Q(fwEx_flag));  // open: en, clr
  Register #(.trigger("falling"), .width(26)) register_25 (
    .D({ID_jmptar, ID_imm16, func}), .clk(clk_brp), .Q(Ex_jtarget[25:0]));  // open: en, clr
  Register #(.trigger("falling"), .width(1)) register_26 (.D(ID_Jump), .clk(clk_brp), .Q(Ex_Jump));  // open: en, clr
  Register #(.trigger("falling"), .width(1)) register_27 (
    .D(ID_Branch), .clk(clk_brp), .Q(Ex_Branch));  // open: en, clr
  Register #(.trigger("falling"), .width(1)) register_28 (
    .D(ID_ExtOp), .clk(clk_brp), .Q(register_28_q));  // open: en, clr
  Register #(.trigger("falling"), .width(1)) register_29 (
    .D(ID_ALUimm), .clk(clk_brp), .Q(register_29_q));  // open: en, clr
  Register #(.trigger("falling"), .width(1)) register_30 (.D(ID_RegWr), .clk(clk_brp), .Q(Ex_RegWr));  // open: en, clr
  Adder #(.width(30)) adder_3 (
    .a({Ex_jtarget[29:26], Ex_nextpc}), .b(bit_extender_4_out), .out(Ex_btarget));  // open: cin, cout
  assign bit_extender_4_out = {{14{register_21_q[15]}}, register_21_q};  // Bit_Extender bit_extender_4
  Multiplexer #(.width(32)) multiplexer_17 (
    .in0(Ex_BusB), .in1(ext_mux_1_out_32), .out(multiplexer_17_out), .sel(register_29_q));
  ext_mux ext_mux_1 (.in_16(register_21_q), .ext_op(register_28_q), .out_32(ext_mux_1_out_32));
  Register #(.trigger("falling"), .width(1)) register_31 (.D(ID_MemWr), .clk(clk_brp), .Q(Ex_MemWr));  // open: en, clr
  Register #(.trigger("falling"), .width(32)) register_32 (.D(out_2), .clk(clk_brp), .Q(out_3));  // open: en, clr
  Register #(.trigger("falling"), .width(32)) register_33 (.D(out_3), .clk(clk_brp), .Q(out_4));  // open: en, clr
  Register #(.trigger("falling"), .width(32)) register_34 (.D(out_4), .clk(clk_brp), .Q(out_5));  // open: en, clr
  Register #(.trigger("falling"), .width(32)) register_35 (.D(out_5), .clk(clk_brp), .Q(out_6));  // open: en, clr
  ALU alu_1 (
    .in_shamt(register_23_q), .in_A(register_19_q), .in_B(multiplexer_17_out), .ALUctr(register_22_q),
    .out_Zero(Ex_Zero), .out_Overflow(Ex_Overflow), .out_Result(Ex_ALUout));
  Register #(.trigger("falling"), .width(1)) register_36 (
    .D(ID_Mem2Reg), .clk(clk_brp), .Q(Ex_Mem2Reg));  // open: en, clr
  Register #(.trigger("falling"), .width(1)) register_37 (.D(ID_Nzero), .clk(clk_brp), .Q(Ex_Nzero));  // open: en, clr
  Register #(.trigger("falling"), .width(32)) register_38 (
    .D(fwMem_ALUout), .clk(clk_brp), .Q(register_38_q));  // open: en, clr
  Register #(.trigger("falling"), .width(1)) register_39 (
    .D(inEx_Mem2Reg), .clk(clk_brp), .Q(register_39_q));  // open: en, clr
  Register #(.trigger("falling"), .width(1)) register_40 (.D(Mem_RegWr), .clk(clk_brp), .Q(Wr_RegWr));  // open: en, clr
  Register #(.trigger("falling"), .width(5)) register_41 (.D(Mem_Rw), .clk(clk_brp), .Q(Wr_Rw));  // open: en, clr
  branch_predictor branch_predictor_1 (
    .result(BrPredictor_result), .WE(BrPredictor_WE), .clk(clk_brp), .clr(in_1), .prediction(BrPredictor_out));
  Register #(.trigger("falling"), .width(5)) register_42 (.D(ID_Rw), .clk(clk_brp), .Q(Ex_Rw));  // open: en, clr
  Multiplexer #(.width(32)) multiplexer_18 (.in0(register_38_q), .in1(Mem_BusW), .out(Wr_data), .sel(register_39_q));

  // Other names for the same wires on the sheet: clk_ex = clk_brp; clk_id = clk_brp; clk_if = clk_brp;
  //   clk_mem = clk_brp; clk_wr = clk_brp; clr = in_1; Ex_instr[31:0] = out_4; Ex_nextpc[29:26] = Ex_jtarget[29:26];
  //   FlushIF0 = BrP_Br; fwEx_ALUout[31:0] = Ex_ALUout; ID_instr[31:0] = out_3; IF_instr[31:0] = out_2;
  //   inEx_ALUout[31:0] = fwMem_ALUout; Mem_ALUout[31:0] = fwMem_ALUout; Mem_Mem2Reg = inEx_Mem2Reg;
  //   ID_imm16[5:0] = func; ID_jmptar[15:0] = {ID_imm16, func}; instr[25:0] = {ID_jmptar, ID_imm16, func};
  //   ID_shamt[4:0] = ID_imm16[10:6]; Rd[4:0] = ID_imm16[15:11]; Rt[4:0] = ID_jmptar[20:16];
  //   Rs[4:0] = ID_jmptar[25:21]; Op[5:0] = instr; FlushID = FlushEx; FlushIF1 = FlushEx; Mem_Br = FlushEx;
  //   Mem_instr[31:0] = out_5; Wr_instr[31:0] = out_6
endmodule

module reg32 (
  input  clear,
  input  [4:0] in_Ra,
  input  [4:0] in_Rb,
  input  [4:0] in_Rw,
  input  in_WE,
  input  [31:0] in_Rwdata,
  input  clk,
  output [31:0] out_Ra,
  output [31:0] out_Rb
);

  wire decoder_1_out0, decoder_1_out1, decoder_1_out2, decoder_1_out3;
  wire [31:0] reg8_0locked_1_out_r1data, reg8_0locked_1_out_r2data, reg8_1_out_r1data, reg8_1_out_r2data,
       reg8_2_out_r1data, reg8_2_out_r2data, reg8_3_out_r1data, reg8_3_out_r2data;

  Decoder #(.select(2)) decoder_1 (
    .out0(decoder_1_out0), .out1(decoder_1_out1), .out2(decoder_1_out2), .out3(decoder_1_out3),
    .sel(in_Rw[4:3]), .en(in_WE));
  reg8_0locked reg8_0locked_1 (
    .in_Rwdata(in_Rwdata), .clk(clk), .in_WE(decoder_1_out0), .in_Rwaddr(in_Rw[2:0]), .clear(clear),
    .in_R1addr(in_Ra[2:0]), .in_R2addr(in_Rb[2:0]), .out_R1data(reg8_0locked_1_out_r1data),
    .out_R2data(reg8_0locked_1_out_r2data));
  reg8 reg8_1 (
    .in_Rwdata(in_Rwdata), .clk(clk), .in_WE(decoder_1_out1), .in_Rwaddr(in_Rw[2:0]), .clear(clear),
    .in_R1addr(in_Ra[2:0]), .in_R2addr(in_Rb[2:0]), .out_R1data(reg8_1_out_r1data),
    .out_R2data(reg8_1_out_r2data));
  reg8 reg8_2 (
    .in_Rwdata(in_Rwdata), .clk(clk), .in_WE(decoder_1_out2), .in_Rwaddr(in_Rw[2:0]), .clear(clear),
    .in_R1addr(in_Ra[2:0]), .in_R2addr(in_Rb[2:0]), .out_R1data(reg8_2_out_r1data),
    .out_R2data(reg8_2_out_r2data));
  reg8 reg8_3 (
    .in_Rwdata(in_Rwdata), .clk(clk), .in_WE(decoder_1_out3), .in_Rwaddr(in_Rw[2:0]), .clear(clear),
    .in_R1addr(in_Ra[2:0]), .in_R2addr(in_Rb[2:0]), .out_R1data(reg8_3_out_r1data),
    .out_R2data(reg8_3_out_r2data));
  Multiplexer #(.select(2), .width(32)) multiplexer_1 (
    .in0(reg8_0locked_1_out_r1data), .in1(reg8_1_out_r1data), .in2(reg8_2_out_r1data),
    .in3(reg8_3_out_r1data), .out(out_Ra), .sel(in_Ra[4:3]));
  Multiplexer #(.select(2), .width(32)) multiplexer_2 (
    .in0(reg8_0locked_1_out_r2data), .in1(reg8_1_out_r2data), .in2(reg8_2_out_r2data),
    .in3(reg8_3_out_r2data), .out(out_Rb), .sel(in_Rb[4:3]));
endmodule

module reg8 (
  input  [31:0] in_Rwdata,
  input  clk,
  input  in_WE,
  input  [2:0] in_Rwaddr,
  input  clear,
  input  [2:0] in_R1addr,
  input  [2:0] in_R2addr,
  output [31:0] out_R1data,
  output [31:0] out_R2data
);

  wire decoder_1_out0, decoder_1_out1, decoder_1_out2, decoder_1_out3, decoder_1_out4, decoder_1_out5,
       decoder_1_out6, decoder_1_out7;
  wire [31:0] reg0_q, reg1_q, reg2_q, reg3_q, reg4_q, reg5_q, reg6_q, reg7_q;

  Decoder #(.select(3)) decoder_1 (
    .out0(decoder_1_out0), .out1(decoder_1_out1), .out2(decoder_1_out2), .out3(decoder_1_out3),
    .out4(decoder_1_out4), .out5(decoder_1_out5), .out6(decoder_1_out6), .out7(decoder_1_out7),
    .sel(in_Rwaddr), .en(in_WE));
  Register #(.trigger("falling"), .width(32)) reg0 (
    .D(in_Rwdata), .en(decoder_1_out0), .clk(clk), .Q(reg0_q), .clr(clear));
  Register #(.trigger("falling"), .width(32)) reg1 (
    .D(in_Rwdata), .en(decoder_1_out1), .clk(clk), .Q(reg1_q), .clr(clear));
  Register #(.trigger("falling"), .width(32)) reg2 (
    .D(in_Rwdata), .en(decoder_1_out2), .clk(clk), .Q(reg2_q), .clr(clear));
  Register #(.trigger("falling"), .width(32)) reg3 (
    .D(in_Rwdata), .en(decoder_1_out3), .clk(clk), .Q(reg3_q), .clr(clear));
  Register #(.trigger("falling"), .width(32)) reg4 (
    .D(in_Rwdata), .en(decoder_1_out4), .clk(clk), .Q(reg4_q), .clr(clear));
  Register #(.trigger("falling"), .width(32)) reg5 (
    .D(in_Rwdata), .en(decoder_1_out5), .clk(clk), .Q(reg5_q), .clr(clear));
  Register #(.trigger("falling"), .width(32)) reg6 (
    .D(in_Rwdata), .en(decoder_1_out6), .clk(clk), .Q(reg6_q), .clr(clear));
  Register #(.trigger("falling"), .width(32)) reg7 (
    .D(in_Rwdata), .en(decoder_1_out7), .clk(clk), .Q(reg7_q), .clr(clear));
  Multiplexer #(.select(3), .width(32)) multiplexer_1 (
    .in0(reg0_q), .in1(reg1_q), .in2(reg2_q), .in3(reg3_q), .in4(reg4_q), .in5(reg5_q), .in6(reg6_q),
    .in7(reg7_q), .out(out_R1data), .sel(in_R1addr));
  Multiplexer #(.select(3), .width(32)) multiplexer_2 (
    .in0(reg0_q), .in1(reg1_q), .in2(reg2_q), .in3(reg3_q), .in4(reg4_q), .in5(reg5_q), .in6(reg6_q),
    .in7(reg7_q), .out(out_R2data), .sel(in_R2addr));
endmodule

module mips_decoder (
  input  [5:0] in_op,
  input  [5:0] in_func,
  output Rtype,
  output RegWr,
  output ALUsrc,
  output RegDst,
  output MemtoReg,
  output MemWr,
  output Branch,
  output Nzero,
  output Jump,
  output ExtOp,
  output [2:0] ALUctl
);

  wire addiu_out, beq_out, not_1_out, not_2_out, not_3_out, not_4_out, not_5_out, not_6_out, not_7_out,
       not_8_out, not_9_out, not_10_out, not_11_out, not_12_out, not_13_out, not_14_out, not_15_out,
       not_16_out, not_17_out, not_18_out, not_19_out, not_20_out, not_21_out, not_22_out, not_23_out,
       not_24_out, not_25_out, not_26_out, not_27_out, not_28_out, not_29_out, not_30_out, not_31_out,
       not_32_out;
  wire [2:0] ALU_ctrler_out;
  wire [2:1] ori_out;

  PLA #(.in_width(6), .out_width(3), .\table ("100000 001\n100010 101\n100011 100\n101010 111\n101011 110\n000000 011 # sll")) ALU_ctrler (
    .in(in_func), .out(ALU_ctrler_out));
  Multiplexer #(.width(3)) multiplexer_1 (.in0({ori_out, 1'b0}), .in1(ALU_ctrler_out), .out(ALUctl), .sel(RegDst));
  or or_1 (ori_out[2], beq_out, Nzero);
  not not_1 (not_1_out, in_op[5]);
  not not_2 (not_2_out, in_op[4]);
  not not_3 (not_3_out, in_op[3]);
  not not_4 (not_4_out, in_op[2]);
  not not_5 (not_5_out, in_op[1]);
  not not_6 (not_6_out, in_op[0]);
  and R_ty (RegDst, not_1_out, not_2_out, not_3_out, not_4_out, not_5_out, not_6_out);
  not not_7 (not_7_out, in_op[5]);
  not not_8 (not_8_out, in_op[4]);
  and ori (ori_out[1], not_7_out, not_8_out, in_op[3], in_op[2], not_10_out, in_op[0]);
  not not_9 (not_9_out, in_op[5]);
  not not_10 (not_10_out, in_op[1]);
  not not_11 (not_11_out, in_op[4]);
  not not_12 (not_12_out, in_op[2]);
  not not_13 (not_13_out, in_op[1]);
  and addiu (addiu_out, not_9_out, not_11_out, in_op[3], not_12_out, not_13_out, in_op[0]);
  not not_14 (not_14_out, in_op[4]);
  not not_15 (not_15_out, in_op[3]);
  not not_16 (not_16_out, in_op[2]);
  and lw (MemtoReg, in_op[5], not_14_out, not_15_out, not_16_out, in_op[1], in_op[0]);
  not not_17 (not_17_out, in_op[4]);
  not not_18 (not_18_out, in_op[2]);
  and sw (MemWr, in_op[5], not_17_out, in_op[3], not_18_out, in_op[1], in_op[0]);
  not not_19 (not_19_out, in_op[5]);
  not not_20 (not_20_out, in_op[4]);
  not not_21 (not_21_out, in_op[3]);
  not not_22 (not_22_out, in_op[1]);
  not not_23 (not_23_out, in_op[0]);
  and beq (beq_out, not_19_out, not_20_out, not_21_out, in_op[2], not_22_out, not_23_out);
  not not_24 (not_24_out, in_op[5]);
  not not_25 (not_25_out, in_op[4]);
  not not_26 (not_26_out, in_op[3]);
  not not_27 (not_27_out, in_op[2]);
  and is_jump (Jump, not_24_out, not_25_out, not_26_out, not_27_out, in_op[1], not_28_out);
  not not_28 (not_28_out, in_op[0]);
  not not_29 (not_29_out, in_op[5]);
  not not_30 (not_30_out, in_op[4]);
  not not_31 (not_31_out, in_op[3]);
  not not_32 (not_32_out, in_op[1]);
  and bne (Nzero, not_29_out, not_30_out, not_31_out, in_op[2], not_32_out, in_op[0]);
  or or_2 (RegWr, RegDst, ori_out[1], addiu_out, MemtoReg);
  or or_3 (ALUsrc, ori_out[1], addiu_out, MemtoReg, MemWr);
  or or_4 (Branch, beq_out, Nzero);
  or or_5 (ExtOp, addiu_out, MemtoReg, MemWr);

  assign Rtype = RegDst;

  // Notes on the sheet:
  //   ALUop
  //   1:sign, 0:zero
endmodule

module reg8_0locked (
  input  [31:0] in_Rwdata,
  input  clk,
  input  in_WE,
  input  [2:0] in_Rwaddr,
  input  clear,
  input  [2:0] in_R1addr,
  input  [2:0] in_R2addr,
  output [31:0] out_R1data,
  output [31:0] out_R2data
);

  wire decoder_1_out1, decoder_1_out2, decoder_1_out3, decoder_1_out4, decoder_1_out5, decoder_1_out6,
       decoder_1_out7;
  wire [31:0] reg0_q, reg1_q, reg2_q, reg3_q, reg4_q, reg5_q, reg6_q, reg7_q;

  Decoder #(.select(3)) decoder_1 (
    .out1(decoder_1_out1), .out2(decoder_1_out2), .out3(decoder_1_out3), .out4(decoder_1_out4),
    .out5(decoder_1_out5), .out6(decoder_1_out6), .out7(decoder_1_out7), .sel(in_Rwaddr), .en(in_WE));  // open: out0
  Register #(.width(32)) reg0 (.clk(clk), .Q(reg0_q), .clr(1'b1));  // open: D, en
  Register #(.width(32)) reg1 (.D(in_Rwdata), .en(decoder_1_out1), .clk(clk), .Q(reg1_q), .clr(clear));
  Register #(.width(32)) reg2 (.D(in_Rwdata), .en(decoder_1_out2), .clk(clk), .Q(reg2_q), .clr(clear));
  Register #(.width(32)) reg3 (.D(in_Rwdata), .en(decoder_1_out3), .clk(clk), .Q(reg3_q), .clr(clear));
  Register #(.width(32)) reg4 (.D(in_Rwdata), .en(decoder_1_out4), .clk(clk), .Q(reg4_q), .clr(clear));
  Register #(.width(32)) reg5 (.D(in_Rwdata), .en(decoder_1_out5), .clk(clk), .Q(reg5_q), .clr(clear));
  Register #(.width(32)) reg6 (.D(in_Rwdata), .en(decoder_1_out6), .clk(clk), .Q(reg6_q), .clr(clear));
  Register #(.width(32)) reg7 (.D(in_Rwdata), .en(decoder_1_out7), .clk(clk), .Q(reg7_q), .clr(clear));
  Multiplexer #(.select(3), .width(32)) multiplexer_1 (
    .in0(reg0_q), .in1(reg1_q), .in2(reg2_q), .in3(reg3_q), .in4(reg4_q), .in5(reg5_q), .in6(reg6_q),
    .in7(reg7_q), .out(out_R1data), .sel(in_R1addr));
  Multiplexer #(.select(3), .width(32)) multiplexer_2 (
    .in0(reg0_q), .in1(reg1_q), .in2(reg2_q), .in3(reg3_q), .in4(reg4_q), .in5(reg5_q), .in6(reg6_q),
    .in7(reg7_q), .out(out_R2data), .sel(in_R2addr));
endmodule

module ext_mux (
  input  [15:0] in_16,
  input  ext_op,
  output [31:0] out_32
);

  wire [31:0] bit_extender_1_out, bit_extender_2_out;

  assign bit_extender_1_out = {{16{1'b0}}, in_16};  // Bit_Extender bit_extender_1
  assign bit_extender_2_out = {{16{in_16[15]}}, in_16};  // Bit_Extender bit_extender_2
  Multiplexer #(.width(32)) multiplexer_1 (
    .in0(bit_extender_1_out), .in1(bit_extender_2_out), .out(out_32), .sel(ext_op));
endmodule

module branch_predictor (
  input  result,
  input  WE,
  input  clk,
  input  clr,
  output prediction
);

  wire and_1_out;
  wire [0:0] register_1_q;
  wire [1:1] multiplexer_1_out;

  Register #(.trigger("falling"), .width(2)) register_1 (
    .D({multiplexer_1_out[1], result}), .en(WE), .clk(clk), .Q({prediction, register_1_q[0]}), .clr(clr));
  Multiplexer multiplexer_1 (.in0(prediction), .in1(result), .out(multiplexer_1_out[1]), .sel(and_1_out));
  and and_1 (and_1_out, result, register_1_q[0]);
endmodule
